// Logisim project sagui_vet.circ as structural Verilog: 9 circuits, main circuit main
module main (
);

  wire and_1_out, Clk, ctrl_1_branch, ctrl_1_regwrs, ctrl_1_regwrv, iszero_1_result, RamWrS, RamWrV,
       SelectR1, UseImm, WbOp;
  wire [1:0] Ra, Rb;
  wire [2:0] AluOp;
  wire [3:0] Instrucoes_data_2;
  wire [3:2] Instrucoes_data;
  wire [7:0] adder_1_out, alu_1_result, alu_2_result, alu_3_result, alu_4_result, alu_5_result,
       banco_reg_1_readdata1, banco_reg_1_readdata2, banco_reg_v_1_readdata1, banco_reg_v_1_readdata2,
       banco_reg_v_2_readdata1, banco_reg_v_2_readdata2, banco_reg_v_3_readdata1, banco_reg_v_3_readdata2,
       banco_reg_v_4_readdata1, banco_reg_v_4_readdata2, Imm, multiplexer_2_out, multiplexer_3_out,
       multiplexer_4_out, multiplexer_5_out, multiplexer_6_out, multiplexer_7_out, multiplexer_8_out,
       multiplexer_9_out, multiplexer_10_out, multiplexer_11_out, multiplexer_12_out, PC_q, ram_1_dout,
       ram_2_dout, ram_3_dout, ram_4_dout, ram_5_dout;

  Register PC (.D(multiplexer_2_out), .en(1'b1), .clk(Clk), .Q(PC_q), .clr(1'b0));
  Clock clock_1 (.out(Clk));
  ROM Instrucoes (.addr(PC_q), .data({Instrucoes_data_2, Instrucoes_data, Rb}));
  Ctrl ctrl_1 (
    .Opcode(Instrucoes_data_2), .AluOp(AluOp), .RegWrV(ctrl_1_regwrv), .RegWrS(ctrl_1_regwrs), .WbOp(WbOp),
    .Branch(ctrl_1_branch), .SelectR1(SelectR1), .UseImm(UseImm), .RamWrV(RamWrV), .RamWrS(RamWrS));
  assign Imm = {{4{Instrucoes_data[3]}}, {Instrucoes_data, Rb}};  // Bit_Extender bit_extender_1
  Multiplexer #(.width(2)) multiplexer_1 (.in0(Instrucoes_data), .in1(2'b01), .out(Ra), .sel(SelectR1));
  Adder adder_1 (.a(PC_q), .b(8'h1), .out(adder_1_out));  // open: cin, cout
  Multiplexer #(.width(8)) multiplexer_2 (
    .in0(adder_1_out), .in1(banco_reg_1_readdata2), .out(multiplexer_2_out), .sel(and_1_out));
  banco_reg_v banco_reg_v_1 (
    .Clk(Clk), .ReadRegister1(Ra), .WriteData(multiplexer_9_out), .ReadRegister2(Rb), .WriteRegister(Ra),
    .RegWrite(ctrl_1_regwrv), .ReadData1(banco_reg_v_1_readdata1), .ReadData2(banco_reg_v_1_readdata2));
  banco_reg_v banco_reg_v_2 (
    .Clk(Clk), .ReadRegister1(Ra), .WriteData(multiplexer_10_out), .ReadRegister2(Rb), .WriteRegister(Ra),
    .RegWrite(ctrl_1_regwrv), .ReadData1(banco_reg_v_2_readdata1), .ReadData2(banco_reg_v_2_readdata2));
  banco_reg_v banco_reg_v_3 (
    .Clk(Clk), .ReadRegister1(Ra), .WriteData(multiplexer_11_out), .ReadRegister2(Rb), .WriteRegister(Ra),
    .RegWrite(ctrl_1_regwrv), .ReadData1(banco_reg_v_3_readdata1), .ReadData2(banco_reg_v_3_readdata2));
  banco_reg_v banco_reg_v_4 (
    .Clk(Clk), .ReadRegister1(Ra), .WriteData(multiplexer_12_out), .ReadRegister2(Rb), .WriteRegister(Ra),
    .RegWrite(ctrl_1_regwrv), .ReadData1(banco_reg_v_4_readdata1), .ReadData2(banco_reg_v_4_readdata2));
  Multiplexer #(.width(8)) multiplexer_3 (
    .in0(banco_reg_v_1_readdata2), .in1(Imm), .out(multiplexer_3_out), .sel(UseImm));
  Multiplexer #(.width(8)) multiplexer_4 (
    .in0(banco_reg_v_2_readdata2), .in1(Imm), .out(multiplexer_4_out), .sel(UseImm));
  Multiplexer #(.width(8)) multiplexer_5 (
    .in0(banco_reg_v_3_readdata2), .in1(Imm), .out(multiplexer_5_out), .sel(UseImm));
  Multiplexer #(.width(8)) multiplexer_6 (
    .in0(banco_reg_v_4_readdata2), .in1(Imm), .out(multiplexer_6_out), .sel(UseImm));
  banco_reg banco_reg_1 (
    .Clk(Clk), .WriteRegister(Ra), .WriteData(multiplexer_8_out), .RegWrite(ctrl_1_regwrs),
    .ReadRegister1(Ra), .ReadRegister2(Rb), .ReadData2(banco_reg_1_readdata2),
    .ReadData1(banco_reg_1_readdata1));
  ALU alu_1 (.Operand1(banco_reg_v_1_readdata1), .Operand2(multiplexer_3_out), .ALUOp(AluOp), .Result(alu_1_result));
  ALU alu_2 (.Operand1(banco_reg_v_2_readdata1), .Operand2(multiplexer_4_out), .ALUOp(AluOp), .Result(alu_2_result));
  ALU alu_3 (.Operand1(banco_reg_v_3_readdata1), .Operand2(multiplexer_5_out), .ALUOp(AluOp), .Result(alu_3_result));
  ALU alu_4 (.Operand1(banco_reg_v_4_readdata1), .Operand2(multiplexer_6_out), .ALUOp(AluOp), .Result(alu_4_result));
  IsZero iszero_1 (.Value(banco_reg_1_readdata1), .Result(iszero_1_result));
  Multiplexer #(.width(8)) multiplexer_7 (
    .in0(banco_reg_1_readdata2), .in1(Imm), .out(multiplexer_7_out), .sel(UseImm));
  and and_1 (and_1_out, ctrl_1_branch, iszero_1_result);
  Multiplexer #(.width(8)) multiplexer_8 (.in0(alu_5_result), .in1(ram_1_dout), .out(multiplexer_8_out), .sel(WbOp));
  Multiplexer #(.width(8)) multiplexer_9 (.in0(alu_1_result), .in1(ram_2_dout), .out(multiplexer_9_out), .sel(WbOp));
  Multiplexer #(.width(8)) multiplexer_10 (.in0(alu_2_result), .in1(ram_3_dout), .out(multiplexer_10_out), .sel(WbOp));
  Multiplexer #(.width(8)) multiplexer_11 (.in0(alu_3_result), .in1(ram_4_dout), .out(multiplexer_11_out), .sel(WbOp));
  Multiplexer #(.width(8)) multiplexer_12 (.in0(alu_4_result), .in1(ram_5_dout), .out(multiplexer_12_out), .sel(WbOp));
  ALU alu_5 (.Operand1(banco_reg_1_readdata1), .Operand2(multiplexer_7_out), .ALUOp(AluOp), .Result(alu_5_result));
  RAM #(.asyncread("true")) ram_1 (
    .addr(multiplexer_7_out), .we(RamWrS), .oe(1'b1), .clk(Clk), .din(alu_5_result), .dout(ram_1_dout));
  RAM #(.asyncread("true")) ram_2 (
    .addr(banco_reg_v_1_readdata2), .we(RamWrV), .oe(1'b1), .clk(Clk), .din(alu_1_result), .dout(ram_2_dout));
  RAM #(.asyncread("true")) ram_3 (
    .addr(banco_reg_v_2_readdata2), .we(RamWrV), .oe(1'b1), .clk(Clk), .din(alu_2_result), .dout(ram_3_dout));
  RAM #(.asyncread("true")) ram_4 (
    .addr(banco_reg_v_3_readdata2), .we(RamWrV), .oe(1'b1), .clk(Clk), .din(alu_3_result), .dout(ram_4_dout));
  RAM #(.asyncread("true")) ram_5 (
    .addr(banco_reg_v_4_readdata2), .we(RamWrV), .oe(1'b1), .clk(Clk), .din(alu_4_result), .dout(ram_5_dout));

  // Notes on the sheet:
  //   contents of Instrucoes (hex, n*v repeats v):
  //   70 80 77 70 87 64 69 6e 99 80 7f 9c 9c a9 ab ac b9 b5 c4 c5 d5 70 81 64 e4 f4 87 e4 f4 51 49 4 70 80
  //   64 8b 72 4 5*0 17 70 80 64 17 6*0 81 74 68 22 7*0 37 6*0 80 70 64 68 6c 8a 64 80 54 81 64 8a 68 99
  //   81 6c 80 51 97 83 7d 51 97 89 71 51 97 8e 73 51 97 82 70 51 97 8e 72 51 97 89 74 51 97 80 72 51 97
  //   8b 70 51 97 81 70 51 8b 7f 52 9b 87 71 52 9b 81 74 52 9b 85 71 52 9b 88 7e 52 9b 8f 7d 52 9b 8f 7f
  //   52 9b 88 71 52 9b 8f 73 52 9b 8a 70 52 81 64 88 71 54 8a 70 68 99 89 71 58 80 72 6c 8a 71 5c 89 70
  //   6c 8b 71 5c 3 88 71 44 89 71 48 8a 71 4c 8b 71 40 94 98 9c 45 4a 96 57 8b 71 44 81 70 a4 8b 71 48 8b
  //   71 54 66 8d 7b 68 86 7e 6c 61 22
  //   Opcode
  //   Ra
  //   Reg / Imm
  //   Rb
  //   pc = pc + 4
  //   pc = rb
endmodule

module banco_reg (
  input  Clk,
  input  [1:0] ReadRegister1,
  input  [7:0] WriteData,
  input  [1:0] ReadRegister2,
  input  [1:0] WriteRegister,
  input  RegWrite,
  output [7:0] ReadData1,
  output [7:0] ReadData2
);

  wire demultiplexer_2_out0, demultiplexer_2_out1, demultiplexer_2_out2, demultiplexer_2_out3;
  wire [7:0] demultiplexer_1_out0, demultiplexer_1_out1, demultiplexer_1_out2, demultiplexer_1_out3,
       register_1_q, register_2_q, register_3_q, register_4_q;

  Demultiplexer #(.select(2), .width(8)) demultiplexer_1 (
    .out0(demultiplexer_1_out0), .out1(demultiplexer_1_out1), .out2(demultiplexer_1_out2),
    .out3(demultiplexer_1_out3), .in(WriteData), .sel(WriteRegister));
  Demultiplexer #(.select(2)) demultiplexer_2 (
    .out0(demultiplexer_2_out0), .out1(demultiplexer_2_out1), .out2(demultiplexer_2_out2),
    .out3(demultiplexer_2_out3), .in(RegWrite), .sel(WriteRegister));
  Register register_1 (.D(demultiplexer_1_out0), .en(demultiplexer_2_out0), .clk(Clk), .Q(register_1_q), .clr(1'b0));
  Register register_2 (.D(demultiplexer_1_out1), .en(demultiplexer_2_out1), .clk(Clk), .Q(register_2_q), .clr(1'b0));
  Register register_3 (.D(demultiplexer_1_out2), .en(demultiplexer_2_out2), .clk(Clk), .Q(register_3_q), .clr(1'b0));
  Register register_4 (.D(demultiplexer_1_out3), .en(demultiplexer_2_out3), .clk(Clk), .Q(register_4_q), .clr(1'b0));
  Multiplexer #(.select(2), .width(8)) multiplexer_1 (
    .in0(register_1_q), .in1(register_2_q), .in2(register_3_q), .in3(register_4_q), .out(ReadData1),
    .sel(ReadRegister1));
  Multiplexer #(.select(2), .width(8)) multiplexer_2 (
    .in0(register_1_q), .in1(register_2_q), .in2(register_3_q), .in3(register_4_q), .out(ReadData2),
    .sel(ReadRegister2));
endmodule

module ALU (
  input  [7:0] Operand1,
  input  [7:0] Operand2,
  input  [2:0] ALUOp,
  output [7:0] Result
);

  wire adder_1_cout, subtractor_1_bout;
  wire [7:0] adder_1_out, and_1_out, or_1_out, subtractor_1_out;

  // NoConnect on Operand2[7:4]
  Adder adder_1 (.a(Operand1), .b(Operand2), .out(adder_1_out), .cin(1'b0), .cout(adder_1_cout));
  Subtractor subtractor_1 (.a(Operand1), .b(Operand2), .out(subtractor_1_out), .bin(1'b0), .bout(subtractor_1_bout));
  assign and_1_out = Operand1 & Operand2;  // AND_Gate and_1, 8 bits wide
  assign or_1_out = Operand1 | Operand2;  // OR_Gate or_1, 8 bits wide
  Multiplexer #(.select(3), .width(8)) multiplexer_1 (
    .in0(adder_1_out), .in1(subtractor_1_out), .in2(and_1_out), .in3(or_1_out),
    .in4({Operand2[3:0], Operand1[3:0]}), .in5({Operand1[7:4], Operand2[3:0]}), .in6({8{1'b0}}),
    .in7({8{1'b0}}), .out(Result), .sel(ALUOp));
  // also tied to GND on the sheet: {adder_1_cout, subtractor_1_bout}

  // Notes on the sheet:
  //   movh
  //   movl
endmodule

module IsZero (
  input  [7:0] Value,
  output Result
);

  and and_1 (Result, 1'b1, ~Value[0], ~Value[1], ~Value[2], ~Value[3], ~Value[4], ~Value[5], ~Value[6], ~Value[7]);  // AND_Gate
endmodule

module Ctrl (
  input  [3:0] Opcode,
  output [2:0] AluOp,
  output RegWrV,
  output RegWrS,
  output WbOp,
  output Branch,
  output SelectR1,
  output UseImm,
  output RamWrV,
  output RamWrS
);

  wire and_2_out, and_3_out, and_4_out, and_5_out, and_6_out, and_7_out, not_1_out, not_3_out, not_4_out;

  not not_1 (not_1_out, Opcode[3]);
  not not_2 (AluOp[2], Opcode[2]);
  not not_3 (not_3_out, Opcode[1]);
  not not_4 (not_4_out, Opcode[0]);
  and and_1 (AluOp[1], Opcode[2], Opcode[1]);
  and and_2 (and_2_out, Opcode[3], not_4_out);
  and and_3 (and_3_out, Opcode[3], Opcode[1]);
  and and_4 (and_4_out, Opcode[3], Opcode[2]);
  and and_5 (and_5_out, not_1_out, not_4_out);
  and and_6 (and_6_out, not_1_out, AluOp[2], Opcode[1]);
  and and_7 (and_7_out, not_1_out, Opcode[2], not_3_out);
  and and_8 (WbOp, AluOp[2], not_3_out);
  and and_9 (Branch, not_1_out, Opcode[2], Opcode[1], Opcode[0]);
  and and_10 (SelectR1, AluOp[2], Opcode[1]);
  and and_11 (UseImm, AluOp[2], Opcode[1]);
  and and_12 (RamWrV, Opcode[3], AluOp[2], not_3_out, Opcode[0]);
  and and_13 (RamWrS, not_1_out, AluOp[2], not_3_out, Opcode[0]);
  or or_1 (RegWrV, and_2_out, and_3_out, and_4_out);
  or or_2 (RegWrS, and_5_out, and_6_out, and_7_out);

  assign AluOp[0] = Opcode[0];
endmodule

module JorB (
  input  [3:0] opcode,
  input  zero,
  output Branch,
  output Jump,
  output RegOrImm
);

  wire not_1_out;

  // NoConnect on opcode[3]
  // NoConnect on opcode[2]
  not not_1 (not_1_out, opcode[1]);
  and and_1 (Branch, not_1_out, zero);

  assign Jump = opcode[1];
  assign RegOrImm = opcode[0];
endmodule

module SelectR0 (
  input  [3:0] Opcode,
  output yes
);

  wire not_1_out, not_2_out, not_3_out;

  not not_1 (not_1_out, Opcode[3]);
  not not_2 (not_2_out, Opcode[2]);
  not not_3 (not_3_out, Opcode[1]);
  and and_1 (yes, not_1_out, not_2_out, not_3_out, Opcode[0]);
endmodule

module BranchCtrl (
  input  [1:0] BranchOp,
  input  JorB,
  input  Zero,
  output [1:0] PcOp
);

  wire and_1_out, and_2_out, and_3_out, and_4_out, not_1_out;

  not not_1 (not_1_out, BranchOp[0]);
  and and_1 (and_1_out, BranchOp[0], JorB, Zero);
  and and_2 (and_2_out, BranchOp[1], BranchOp[0], JorB);
  and and_3 (and_3_out, not_1_out, JorB, Zero);
  and and_4 (and_4_out, BranchOp[1], not_1_out, JorB);
  or or_1 (PcOp[1], and_1_out, and_2_out);
  or or_2 (PcOp[0], and_3_out, and_4_out);
endmodule

module banco_reg_v (
  input  Clk,
  input  [1:0] ReadRegister1,
  input  [7:0] WriteData,
  input  [1:0] ReadRegister2,
  input  [1:0] WriteRegister,
  input  RegWrite,
  output [7:0] ReadData1,
  output [7:0] ReadData2
);

  wire demultiplexer_2_out0, demultiplexer_2_out1, demultiplexer_2_out2, demultiplexer_2_out3;
  wire [7:0] demultiplexer_1_out0, demultiplexer_1_out1, demultiplexer_1_out2, demultiplexer_1_out3,
       register_1_q, register_2_q, register_3_q, register_4_q;

  Demultiplexer #(.select(2), .width(8)) demultiplexer_1 (
    .out0(demultiplexer_1_out0), .out1(demultiplexer_1_out1), .out2(demultiplexer_1_out2),
    .out3(demultiplexer_1_out3), .in(WriteData), .sel(WriteRegister));
  Demultiplexer #(.select(2)) demultiplexer_2 (
    .out0(demultiplexer_2_out0), .out1(demultiplexer_2_out1), .out2(demultiplexer_2_out2),
    .out3(demultiplexer_2_out3), .in(RegWrite), .sel(WriteRegister));
  Register register_1 (.D(demultiplexer_1_out0), .en(demultiplexer_2_out0), .clk(Clk), .Q(register_1_q), .clr(1'b0));
  Register register_2 (.D(demultiplexer_1_out1), .en(demultiplexer_2_out1), .clk(Clk), .Q(register_2_q), .clr(1'b0));
  Register register_3 (.D(demultiplexer_1_out2), .en(demultiplexer_2_out2), .clk(Clk), .Q(register_3_q), .clr(1'b0));
  Register register_4 (.D(demultiplexer_1_out3), .en(demultiplexer_2_out3), .clk(Clk), .Q(register_4_q), .clr(1'b0));
  Multiplexer #(.select(2), .width(8)) multiplexer_1 (
    .in0(register_1_q), .in1(register_2_q), .in2(register_3_q), .in3(register_4_q), .out(ReadData1),
    .sel(ReadRegister1));
  Multiplexer #(.select(2), .width(8)) multiplexer_2 (
    .in0(register_1_q), .in1(register_2_q), .in2(register_3_q), .in3(register_4_q), .out(ReadData2),
    .sel(ReadRegister2));
endmodule
